# Fritzing sketch FreeRTOS_led (saved by Fritzing 0.9.3b)
breadboards: 1

parts:
  Part1 = Arduino Uno (Rev3)
  LED1 = LED - 5mm [color="Red (633nm)" package="5 mm [THT]"]
  LED2 = LED - 5mm [color="Yellow (592nm)" package="5 mm [THT]"]
  LED3 = LED - 5mm [color="Green (565nm)" package="5 mm [THT]"]
  R1 = Resistor [tolerance=±5% resistance=220 package=THT]
  R2 = Resistor [tolerance=±5% resistance=220 package=THT]
  R3 = Resistor [tolerance=±5% resistance=220 package=THT]
  LED4 = LED - 5mm [color="Blue (470nm)" package="5 mm [THT]"]
  R4 = Resistor [tolerance=±5% resistance=220 package=THT]
  Sensor_PIR_HC-SR502 = HC-SR501 Body Sensor Module

nets:
  N1: Part1.D12/MISO, Sensor_PIR_HC-SR502.OUT
  GND: Part1.GND, R1.Pin_0, R2.Pin_0, R3.Pin_0, R4.Pin_0, Sensor_PIR_HC-SR502.GND
  N2: Part1.D3_PWM, LED2.anode
  N3: Part1.D4, LED1.anode
  N4: Part1.D5_PWM, LED3.anode
  N5: Part1.D6_PWM, LED4.anode
  5V: Part1.5V, Sensor_PIR_HC-SR502.VCC
  N6: LED1.cathode, R2.Pin_1
  N7: LED2.cathode, R1.Pin_1
  N8: LED3.cathode, R3.Pin_1
  N9: LED4.cathode, R4.Pin_1

custom parts:
  HC-SR501 Body Sensor Module: Pyroelectric Infrared PIR Motion Sensor Detector Module
